# Fritzing sketch senzor sr-04 (saved by Fritzing 0.9.3b)
breadboards: 1

parts:
  Parte1 = Arduino Uno (Rev3)
  Raspberry_Pi2 = Raspberry Pi 2  # not connected
  LED1 = smd LED [color="Green (555nm)" package="0603 [SMD]"]
  LED2 = smd LED [color="Red (660nm)" package="0603 [SMD]"]
  R1 = Resistor [tolerance=±5% resistance=100 package="0805 [SMD]"]
  R2 = Resistor [tolerance=±5% resistance=100 package="0805 [SMD]"]
  hc-sr1 = hc-sr04

nets:
  N1: Parte1.D10_PWM/SS, LED1.anode
  N2: Parte1.D11_PWM/MOSI, LED2.anode
  N3: Parte1.D12/MISO, hc-sr1.Echo
  N4: Parte1.D13/SCK, hc-sr1.Trig
  5V: Parte1.5V, hc-sr1.VCC
  GND: Parte1.GND, R1.Pin_1, R2.Pin_1, hc-sr1.GND
  N5: LED1.cathode, R2.Pin_0
  N6: LED2.cathode, R1.Pin_0

notes:
  Comunicare serial prin usb
  rezistori 100 (ohm)
